// Digital circuit 10x16SRam.dig as structural Verilog
module _10x16SRam (
  input  [3:0] WA_3_0,
  input  WE,
  input  [15:0] WRD_15_0,
  input  [3:0] RA1_3_0,
  input  [3:0] RA2_3_0,
  input  CLOCK,
  output [15:0] RD1_15_0,
  output [15:0] RD2_15_0
);

  wire R1_0, R1_1, R1_2, R1_3, R1_4, R1_5, R1_6, R1_7, R1_8, R1_9, R2_0, R2_1, R2_2, R2_3, R2_4, R2_5, R2_6,
       R2_7, R2_8, R2_9, W0, W1, W2, W3, W4, W5, W6, W7, W8, W9, WS0, WS1, WS2, WS3, WS4, WS5, WS6, WS7, WS8,
       WS9;
  wire [15:0] RD1_0, RD1_1, RD1_2, RD1_3, RD1_4, RD1_5, RD1_6, RD1_7, RD1_8, RD1_9, RD2_0, RD2_1, RD2_2,
       RD2_3, RD2_4, RD2_5, RD2_6, RD2_7, RD2_8, RD2_9;

  and and_1 (WS0, W0, WE);
  and and_2 (WS2, W2, WE);
  and and_3 (WS4, W4, WE);
  and and_4 (WS6, W6, WE);
  and and_5 (WS8, W8, WE);
  Decoder #(.Selector_Bits(4)) decoder_1 (
    .sel(RA1_3_0), .out_0(R1_0), .out_1(R1_1), .out_2(R1_2), .out_3(R1_3), .out_4(R1_4), .out_5(R1_5),
    .out_6(R1_6), .out_7(R1_7), .out_8(R1_8), .out_9(R1_9));  // open: out_10, out_11, out_12, out_13, out_14, out_15
  Decoder #(.Selector_Bits(4)) decoder_2 (
    .sel(RA2_3_0), .out_0(R2_0), .out_1(R2_1), .out_2(R2_2), .out_3(R2_3), .out_4(R2_4), .out_5(R2_5),
    .out_6(R2_6), .out_7(R2_7), .out_8(R2_8), .out_9(R2_9));  // open: out_10, out_11, out_12, out_13, out_14, out_15
  Decoder #(.Selector_Bits(4)) decoder_3 (
    .sel(WA_3_0), .out_0(W0), .out_1(W1), .out_2(W2), .out_3(W3), .out_4(W4), .out_5(W5), .out_6(W6),
    .out_7(W7), .out_8(W8), .out_9(W9));  // open: out_10, out_11, out_12, out_13, out_14, out_15
  and and_6 (WS1, W1, WE);
  and and_7 (WS3, W3, WE);
  and and_8 (WS5, W5, WE);
  and and_9 (WS7, W7, WE);
  and and_10 (WS9, W9, WE);
  _1X16SRam _1x16sram_1 (
    .RS1(R1_9), .RS2(R2_9), .WS(WS9), .WD_15_0(WRD_15_0), .Clock(CLOCK), .RD1_15_0(RD1_9), .RD2_15_0(RD2_9));
  _1X16SRam _1x16sram_2 (
    .RS1(R1_8), .RS2(R2_8), .WS(WS8), .WD_15_0(WRD_15_0), .Clock(CLOCK), .RD1_15_0(RD1_8), .RD2_15_0(RD2_8));
  _1X16SRam _1x16sram_3 (
    .RS1(R1_7), .RS2(R2_7), .WS(WS7), .WD_15_0(WRD_15_0), .Clock(CLOCK), .RD1_15_0(RD1_7), .RD2_15_0(RD2_7));
  _1X16SRam _1x16sram_4 (
    .RS1(R1_6), .RS2(R2_6), .WS(WS6), .WD_15_0(WRD_15_0), .Clock(CLOCK), .RD1_15_0(RD1_6), .RD2_15_0(RD2_6));
  _1X16SRam _1x16sram_5 (
    .RS1(R1_5), .RS2(R2_5), .WS(WS5), .WD_15_0(WRD_15_0), .Clock(CLOCK), .RD1_15_0(RD1_5), .RD2_15_0(RD2_5));
  _1X16SRam _1x16sram_6 (
    .RS1(R1_4), .RS2(R2_4), .WS(WS4), .WD_15_0(WRD_15_0), .Clock(CLOCK), .RD1_15_0(RD1_4), .RD2_15_0(RD2_4));
  _1X16SRam _1x16sram_7 (
    .RS1(R1_3), .RS2(R2_3), .WS(WS3), .WD_15_0(WRD_15_0), .Clock(CLOCK), .RD1_15_0(RD1_3), .RD2_15_0(RD2_3));
  _1X16SRam _1x16sram_8 (
    .RS1(R1_2), .RS2(R2_2), .WS(WS2), .WD_15_0(WRD_15_0), .Clock(CLOCK), .RD1_15_0(RD1_2), .RD2_15_0(RD2_2));
  _1X16SRam _1x16sram_9 (
    .RS1(R1_1), .RS2(R2_1), .WS(WS1), .WD_15_0(WRD_15_0), .Clock(CLOCK), .RD1_15_0(RD1_1), .RD2_15_0(RD2_1));
  _1X16SRam _1x16sram_10 (
    .RS1(R1_0), .RS2(R2_0), .WS(WS0), .WD_15_0(WRD_15_0), .Clock(CLOCK), .RD1_15_0(RD1_0), .RD2_15_0(RD2_0));
  assign RD1_15_0 = RD1_9 | RD1_8 | RD1_7 | RD1_6 | RD1_5 | RD1_4 | RD1_3 | RD1_2 | RD1_1 | RD1_0;  // Or or_1, 16 bits wide
  assign RD2_15_0 = RD2_9 | RD2_8 | RD2_7 | RD2_6 | RD2_5 | RD2_4 | RD2_3 | RD2_2 | RD2_1 | RD2_0;  // Or or_2, 16 bits wide

  // Other names for the same wires on the sheet: CLK = CLOCK; WRD[15:0] = WRD_15_0
endmodule
