// Digital circuit 4BitCPU.dig as structural Verilog
module _4BitCPU (
  input  WE,
  input  [15:0] WRD_15_0,
  input  CLOCK,
  input  [3:0] WA_3_0,
  input  CPU_EN,
  input  [3:0] RA2_3_0,
  input  ZF,
  input  CF,
  output [15:0] RD2_15_0,
  output [1:0] R1_1_0,
  output [1:0] R2_1_0,
  output [1:0] WR_1_0,
  output [3:0] B_3_0,
  output [3:0] A_3_0,
  output [3:0] R_3_0,
  output [3:0] VAL_3_0
);

  wire CPU_CLK, Imm_Sel, JMP_SEL, REG_EN;
  wire [1:0] OP_s;
  wire [3:0] _4bit_adder_1_o_3_0, _4bitpc_1_o_3_0, _4bitregset_1_b_3_0, _10x16sram_1_rd1_15_0,
       multiplexer_1_out;
  wire [5:0] Dont_Care;

  Multiplexer #(.Bits(4)) multiplexer_1 (
    .sel(JMP_SEL), .in_0(_4bit_adder_1_o_3_0), .in_1({R1_1_0, R2_1_0}), .out(multiplexer_1_out));
  _4bitPC _4bitpc_1 (.I__3_0(multiplexer_1_out), .Clock(CPU_CLK), .O_3_0(_4bitpc_1_o_3_0));
  _4bit_Adder _4bit_adder_1 (.I__3_0(_4bitpc_1_o_3_0), .O_3_0(_4bit_adder_1_o_3_0));
  and and_1 (CPU_CLK, CPU_EN, CLOCK);
  _10x16SRam _10x16sram_1 (
    .RA1_3_0(_4bitpc_1_o_3_0), .RA2_3_0(RA2_3_0), .WA_3_0(WA_3_0), .WE(WE), .WRD_15_0(WRD_15_0),
    .CLOCK(CLOCK), .RD1_15_0({_10x16sram_1_rd1_15_0, R1_1_0, R2_1_0, VAL_3_0[1:0], Dont_Care}),
    .RD2_15_0(RD2_15_0));
  _4bitRegSet _4bitregset_1 (
    .WR_1_0(R1_1_0), .Clock(CPU_CLK), .WE(REG_EN), .WRD_3_0(R_3_0), .A_3_0(A_3_0),
    .B_3_0(_4bitregset_1_b_3_0), .RA_1_0(R1_1_0), .RB_1_0(R2_1_0));
  _4bitALU _4bitalu_1 (.X_3_0(A_3_0), .Y_3_0(B_3_0), .R_3_0(R_3_0), .OP_1_0(OP_s));
  Control_unit control_unit_1 (
    .Op_3_0(_10x16sram_1_rd1_15_0), .ZF(ZF), .SF(CF), .Op_1_0(OP_s), .Reg_En(REG_EN), .Imm_sel(Imm_Sel),
    .JMP_SEL(JMP_SEL));
  Multiplexer #(.Bits(4)) multiplexer_2 (
    .sel(Imm_Sel), .in_0(_4bitregset_1_b_3_0), .in_1({R2_1_0, VAL_3_0[1:0]}), .out(B_3_0));

  assign VAL_3_0[3:2] = R2_1_0;
  assign WR_1_0 = R1_1_0;

  // Other names for the same wires on the sheet: Dont_Care[7:6] = VAL_3_0[1:0]; Val[3:0] = {R2_1_0, VAL_3_0[1:0]};
  //   JMP_addrs[3:0] = {R1_1_0, R2_1_0}; R2[1:0] = R2_1_0; R1[1:0] = R1_1_0; A[3:0] = A_3_0; B[3:0] = B_3_0;
  //   CLK = CLOCK; RD2[15:0] = RD2_15_0

  // Notes on the sheet:
  //   Register Mode(Type of OP = 00) = 2bit(Type of OPs) + 2bit(OPs) + 2bit (Reg1)+ 2bit(Reg2)+ 8bits(Dont Care)
  //   Immediate Mode(Type of OP = 01) = 2bit(Type of OPs) + 2bit(OPs) + 2bit (Reg1)+ 4bit(Imm Value)+ 6bits(Dont Care)
  //   Jump Mode(Type of OP = 10) = 2bit(Type of OPs) + 2bit(OPs) + 4bit(JMP addrs)+ 8bits(Dont Care)
  //   OpCode operations: 
  //   	Add (OP=00), NOT (OP=01), SHL (OP=10), JMP (OP=00), JLE (OP=01)
  //   ADD R1,R1 = 00  00   01  01  00000000
  //   NOT R1 =      00  01   01  00   00000000
  //   SHL R1, R2= 00  01   01  00   00000000
  //   ADD R1,5 = 0100010101000000
  //   JMP LABEL = 10 00 0100 00000000
  //   JLE LABEL = 1001010100000000
endmodule
