// Digital circuit 4bitALU.dig as structural Verilog
module _4bitALU (
  input  [3:0] X_3_0,
  input  [3:0] Y_3_0,
  input  [1:0] OP_1_0,
  output [3:0] R_3_0
);

  wire [3:0] _4bitadder_1_s_3_0, _4bitnot_1_s_3_0, _4bitshl_1_s_3_0;

  _4bitAdder _4bitadder_1 (.X_3_0(X_3_0), .Y_3_0(Y_3_0), .S_3_0(_4bitadder_1_s_3_0));  // open: Cout
  _4bitNot _4bitnot_1 (.X_3_0(X_3_0), .S_3_0(_4bitnot_1_s_3_0));
  _4bitSHL _4bitshl_1 (.X_3_0(X_3_0), .Y_3_0(Y_3_0), .S_3_0(_4bitshl_1_s_3_0));
  Multiplexer #(.Selector_Bits(2), .Bits(4)) multiplexer_1 (
    .sel(OP_1_0), .in_0(_4bitadder_1_s_3_0), .in_1(_4bitnot_1_s_3_0), .in_2(_4bitshl_1_s_3_0),
    .in_3(4'b0000), .out(R_3_0));

  // Other names for the same wires on the sheet: x[3:0] = X_3_0; y[3:0] = Y_3_0
endmodule
