// Digital circuit 4bitAdder.dig as structural Verilog
module _4bitAdder (
  input  [3:0] X_3_0,
  input  [3:0] Y_3_0,
  output [3:0] S_3_0,
  output Cout
);

  wire fa_2_cout, fa_3_cout, fa_4_cout;

  FA fa_1 (.X(X_3_0[3]), .Y(Y_3_0[3]), .Cin(fa_2_cout), .S(S_3_0[3]), .Cout(Cout));
  FA fa_2 (.X(X_3_0[2]), .Y(Y_3_0[2]), .Cin(fa_3_cout), .S(S_3_0[2]), .Cout(fa_2_cout));
  FA fa_3 (.X(X_3_0[1]), .Y(Y_3_0[1]), .Cin(fa_4_cout), .S(S_3_0[1]), .Cout(fa_3_cout));
  FA fa_4 (.X(X_3_0[0]), .Y(Y_3_0[0]), .Cin(1'b0), .S(S_3_0[0]), .Cout(fa_4_cout));
endmodule
