// Digital circuit 4bitNot.dig as structural Verilog
module _4bitNot (
  input  [3:0] X_3_0,
  output [3:0] S_3_0
);

  not not_1 (S_3_0[0], X_3_0[0]);
  not not_2 (S_3_0[1], X_3_0[1]);
  not not_3 (S_3_0[2], X_3_0[2]);
  not not_4 (S_3_0[3], X_3_0[3]);
endmodule
