// Digital circuit 4bitPC.dig as structural Verilog
module _4bitPC (
  input  [3:0] I__3_0,
  input  Clock,
  output [3:0] O_3_0
);

  _4BitReg _4bitreg_1 (.Din_3_0(I__3_0), .Sel(1'b1), .Clock(Clock), .Dout_3_0(O_3_0));

  // Other names for the same wires on the sheet: CLK = Clock; I[3:0] = I__3_0
endmodule
