// Digital circuit 4bitRegSet.dig as structural Verilog
module _4bitRegSet (
  input  [1:0] WR_1_0,
  input  WE,
  input  [3:0] WRD_3_0,
  input  Clock,
  input  [1:0] RA_1_0,
  input  [1:0] RB_1_0,
  output [3:0] A_3_0,
  output [3:0] B_3_0
);

  wire A0, A1, A2, A3, D0, D1, D2, D3;
  wire [3:0] R0, R1, R2, R3;

  Decoder #(.Selector_Bits(2)) decoder_1 (.sel(WR_1_0), .out_0(A0), .out_1(A1), .out_2(A2), .out_3(A3));
  and and_1 (D0, A0, WE);
  and and_2 (D2, A2, WE);
  and and_3 (D1, A1, WE);
  and and_4 (D3, A3, WE);
  _4BitReg _4bitreg_1 (.Din_3_0(WRD_3_0), .Sel(D3), .Clock(Clock), .Dout_3_0(R3));
  _4BitReg _4bitreg_2 (.Din_3_0(WRD_3_0), .Sel(D2), .Clock(Clock), .Dout_3_0(R2));
  _4BitReg _4bitreg_3 (.Din_3_0(WRD_3_0), .Sel(D1), .Clock(Clock), .Dout_3_0(R1));
  _4BitReg _4bitreg_4 (.Din_3_0(WRD_3_0), .Sel(D0), .Clock(Clock), .Dout_3_0(R0));
  Multiplexer #(.Selector_Bits(2), .Bits(4)) multiplexer_1 (
    .sel(RA_1_0), .in_0(R0), .in_1(R1), .in_2(R2), .in_3(R3), .out(A_3_0));
  Multiplexer #(.Selector_Bits(2), .Bits(4)) multiplexer_2 (
    .sel(RB_1_0), .in_0(R0), .in_1(R1), .in_2(R2), .in_3(R3), .out(B_3_0));

  // Other names for the same wires on the sheet: RA[1:0] = RA_1_0; RB[1:0] = RB_1_0; WRD[3:0] = WRD_3_0
endmodule
