// Digital circuit 4bitSHL.dig as structural Verilog
module _4bitSHL (
  input  [3:0] X_3_0,
  input  [3:0] Y_3_0,
  output [3:0] S_3_0
);

  Multiplexer #(.Selector_Bits(4)) multiplexer_1 (
    .sel(Y_3_0), .in_0(X_3_0[3]), .in_1(X_3_0[2]), .in_2(X_3_0[1]), .in_3(X_3_0[0]), .in_4(1'b0),
    .in_5(1'b0), .in_6(1'b0), .in_7(1'b0), .in_8(1'b0), .in_9(1'b0), .in_10(1'b0), .in_11(1'b0),
    .in_12(1'b0), .in_13(1'b0), .in_14(1'b0), .in_15(1'b0), .out(S_3_0[3]));
  Multiplexer #(.Selector_Bits(4)) multiplexer_2 (
    .sel(Y_3_0), .in_0(X_3_0[2]), .in_1(X_3_0[1]), .in_2(X_3_0[0]), .in_3(1'b0), .in_4(1'b0), .in_5(1'b0),
    .in_6(1'b0), .in_7(1'b0), .in_8(1'b0), .in_9(1'b0), .in_10(1'b0), .in_11(1'b0), .in_12(1'b0),
    .in_13(1'b0), .in_14(1'b0), .in_15(1'b0), .out(S_3_0[2]));
  Multiplexer #(.Selector_Bits(4)) multiplexer_3 (
    .sel(Y_3_0), .in_0(X_3_0[1]), .in_1(X_3_0[0]), .in_2(1'b0), .in_3(1'b0), .in_4(1'b0), .in_5(1'b0),
    .in_6(1'b0), .in_7(1'b0), .in_8(1'b0), .in_9(1'b0), .in_10(1'b0), .in_11(1'b0), .in_12(1'b0),
    .in_13(1'b0), .in_14(1'b0), .in_15(1'b0), .out(S_3_0[1]));
  Multiplexer #(.Selector_Bits(4)) multiplexer_4 (
    .sel(Y_3_0), .in_0(X_3_0[0]), .in_1(1'b0), .in_2(1'b0), .in_3(1'b0), .in_4(1'b0), .in_5(1'b0),
    .in_6(1'b0), .in_7(1'b0), .in_8(1'b0), .in_9(1'b0), .in_10(1'b0), .in_11(1'b0), .in_12(1'b0),
    .in_13(1'b0), .in_14(1'b0), .in_15(1'b0), .out(S_3_0[0]));

  // Other names for the same wires on the sheet: Sel[3:0] = Y_3_0; A0 = X_3_0[0]; A1 = X_3_0[1]; A2 = X_3_0[2];
  //   A3 = X_3_0[3]
endmodule
