// Digital circuit Control_unit.dig as structural Verilog
module Control_unit (
  input  [3:0] Op_3_0,
  input  ZF,
  input  SF,
  output Reg_En,
  output Imm_sel,
  output [1:0] Op_1_0,
  output JMP_SEL
);

  wire and_1_out, and_3_out, and_4_out, and_5_out, or_1_out, or_3_out;

  or or_1 (or_1_out, ZF, SF);
  and and_1 (and_1_out, ~Op_3_0[2], ~Op_3_0[3]);  // And
  and and_2 (Imm_sel, Op_3_0[2], ~Op_3_0[3]);  // And
  and and_3 (and_3_out, ~Op_3_0[2], Op_3_0[3]);  // And
  and and_4 (and_4_out, ~Op_3_0[0], ~Op_3_0[1]);  // And
  and and_5 (and_5_out, Op_3_0[0], ~Op_3_0[1], or_1_out);  // And
  or or_2 (Reg_En, and_1_out, Imm_sel);
  or or_3 (or_3_out, and_4_out, and_5_out);
  and and_6 (JMP_SEL, and_3_out, or_3_out);

  assign Op_1_0 = Op_3_0[1:0];
endmodule
